# Fritzing sketch FFheaterControler (saved by Fritzing 1.0.7)
breadboards: 1

parts:
  R1 = Resistor [tolerance=±5% resistance=220 package="2512 [SMD]"]
  R2 = Resistor [tolerance=±5% resistance=220 package="2512 [SMD]"]
  R3 = Resistor [tolerance=±5% resistance=220 package="2512 [SMD]"]
  R4 = Resistor [tolerance=±5% resistance=220 package="2512 [SMD]"]
  DHT1 = DHT11 Humitidy and Temperature Sensor (3 pins)
  DHT2 = DHT11 Humitidy and Temperature Sensor (3 pins)
  S1 = SWITCH-MOMENTARY-2 [package=tactile-pth-12mm]
  S2 = SWITCH-MOMENTARY-2 [package=tactile-pth-12mm]
  S3 = SWITCH-MOMENTARY-2 [package=tactile-pth-12mm]
  S4 = SWITCH-MOMENTARY-2 [package=tactile-pth-12mm]
  C2 = Ceramic Capacitor [capacitance=100nF package="100 mil [THT, multilayer]"]
  C3 = Ceramic Capacitor [capacitance=100nF package="100 mil [THT, multilayer]"]
  U2 = LIPO-1000mAh [package=lipo-1000]
  S5 = Toggle Switch [package=THT]
  U3 = Sharp PC817 [package=THT]
  U4 = Sharp PC817 [package=THT]
  U5 = Sharp PC817 [package=THT]
  U6 = Sharp PC817 [package=THT]
  M1 = MT3608 Module
  U7 = ESP32S-HiLetgo [part_number=ESP32S-HiLetgo]

nets (from the breadboard view):
  N1: R1.Pin_0, U5.Pin_1
  N2: R1.Pin_1, U7.GPIO26
  N3: R2.Pin_0, U4.Pin_1
  N4: R2.Pin_1, U7.GPIO32
  N5: R3.Pin_0, U6.Pin_1
  N6: R3.Pin_1, U7.GPIO27
  N7: R4.Pin_0, U3.Pin_1
  N8: R4.Pin_1, U7.GPIO25
  N9: DHT1.Plus, DHT2.Plus, C2.0, C3.0, M1.pin3
  N10: DHT1.Signal, U7.GPIO17
  GND: DHT1.Gnd, DHT2.Gnd, C2.1, C3.1, U3.Pin_2, U4.Pin_2, U5.Pin_2, U6.Pin_2, M1.pin4
  N11: DHT2.Signal, U7.GPIO5
  N12: S1.1, U3.Pin_4
  N13: S2.1, U4.Pin_4
  N14: S3.1, U5.Pin_4
  N15: S4.1, U6.Pin_4
  N16: U2.+, S5.L1
  N17: U2.-, M1.pin1
  N18: S5.COM, M1.pin2

custom parts:
  DHT11 Humitidy and Temperature Sensor (3 pins): DHT11 Humidity and Temperature Sensor (3 pins).
  MT3608 Module: MT3608 Boost Converter Module Links: Aerosemi MT3608 2A Step Up Converter datasheet
  ESP32S-HiLetgo: HiLetgo ESP-WROOM-32 ESP32 ESP-32S Development Board 2.4GHz Dual-Mode WiFi + Bluetooth Dual Cores Microcontroller The ESP32 integrated with Antenna switches, RF Balun, power amplifiers, low-noise amplifiers, filters, and management modules, and the entire solution occupies the least area of PCB. 2.4 GHz Wi-Fi plus Bluetooth dual-mode chip, with TSMC Ultra-low power consumption 40nm technology,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
